// Logisim project 5BitAdder.circ as structural Verilog: 3 circuits, main circuit main
module main (
  input  in_1,
  input  [4:0] in_2,
  input  [4:0] in_3,
  output [4:0] out_4
);

  _5BitAdder u_5bitadder_1 (.in_1(in_1), .in_2(in_2), .in_3(in_3), .out_4(out_4));
endmodule

module _1BitAdder (
  input  C_In,
  input  A,
  input  B,
  output Sum,
  output C_Out
);

  wire and_1_out, and_2_out, and_3_out, and_4_out, and_5_out, not_1_out, xnor_1_out, xor_1_out;

  not not_1 (not_1_out, C_In);
  and and_1 (and_1_out, C_In, B);
  and and_2 (and_2_out, A, C_In);
  and and_3 (and_3_out, A, B);
  xnor xnor_1 (xnor_1_out, A, B);
  xor xor_1 (xor_1_out, B, A);
  and and_4 (and_4_out, C_In, xnor_1_out);
  and and_5 (and_5_out, not_1_out, xor_1_out);
  or or_1 (C_Out, and_1_out, and_2_out, and_3_out);
  or or_2 (Sum, and_4_out, and_5_out);

  // Notes on the sheet:
  //   C = C_IN AND (A XNOR B) OR NOTC_IN (A XOR B)
  //   C_OUT = (A AND B) OR (A AND C_IN) OR (B AND C_IN)
  //   C = C_IN AND (NOTA AND NOTB OR A AND B) OR NOTC_IN AND (NOTA AND B OR A AND NOTB)
  //   C = (NOTA AND NOTB AND C_IN) OR (A AND NOTB AND NOTC_IN) OR (NOTA AND B AND NOTC_IN) OR (A AND B AND C_IN)
endmodule

module _5BitAdder (
  input  in_1,
  input  [4:0] in_2,
  input  [4:0] in_3,
  output [4:0] out_4
);

  wire n1bitadder_1_c_out, n1bitadder_2_c_out, n1bitadder_3_c_out, n1bitadder_4_c_out;

  _1BitAdder u_1bitadder_1 (.C_In(in_1), .A(in_2[0]), .B(in_3[0]), .Sum(out_4[0]), .C_Out(n1bitadder_1_c_out));
  _1BitAdder u_1bitadder_2 (
    .C_In(n1bitadder_1_c_out), .A(in_2[1]), .B(in_3[1]), .Sum(out_4[1]), .C_Out(n1bitadder_2_c_out));
  _1BitAdder u_1bitadder_3 (
    .C_In(n1bitadder_2_c_out), .A(in_2[2]), .B(in_3[2]), .Sum(out_4[2]), .C_Out(n1bitadder_3_c_out));
  _1BitAdder u_1bitadder_4 (
    .C_In(n1bitadder_3_c_out), .A(in_2[3]), .B(in_3[3]), .Sum(out_4[3]), .C_Out(n1bitadder_4_c_out));
  _1BitAdder u_1bitadder_5 (.C_In(n1bitadder_4_c_out), .A(in_2[4]), .B(in_3[4]), .Sum(out_4[4]));  // open: C_Out
endmodule
