// Logisim project AddingCircuitWithDisplay.circ as structural Verilog: 8 circuits, main circuit main
module main (
  input  in_1,
  input  [4:0] in_2,
  input  [4:0] in_3
);

  wire [6:0] n5bitadderdisplay_1_out_4, n5bitadderdisplay_1_out_5;

  _5BitAdderDisplay u_5bitadderdisplay_1 (
    .in_1(in_1), .A(in_2), .B(in_3), .out_4(n5bitadderdisplay_1_out_4), .out_5(n5bitadderdisplay_1_out_5));
  _7_Segment_Display u_7_segment_display_1 (
    .g(n5bitadderdisplay_1_out_4[3]), .f(n5bitadderdisplay_1_out_4[2]), .a(n5bitadderdisplay_1_out_4[0]),
    .b(n5bitadderdisplay_1_out_4[1]), .e(n5bitadderdisplay_1_out_4[4]), .d(n5bitadderdisplay_1_out_4[5]),
    .c(n5bitadderdisplay_1_out_4[6]));  // open: dp
  _7_Segment_Display u_7_segment_display_2 (
    .g(n5bitadderdisplay_1_out_5[3]), .f(n5bitadderdisplay_1_out_5[2]), .a(n5bitadderdisplay_1_out_5[0]),
    .b(n5bitadderdisplay_1_out_5[1]), .e(n5bitadderdisplay_1_out_5[4]), .d(n5bitadderdisplay_1_out_5[5]),
    .c(n5bitadderdisplay_1_out_5[6]));  // open: dp
endmodule

module _1BitAdder (
  input  C_In,
  input  A,
  input  B,
  output Sum,
  output C_Out
);

  wire and_1_out, and_2_out, and_3_out, and_4_out, and_5_out, not_1_out, xnor_1_out, xor_1_out;

  not not_1 (not_1_out, C_In);
  and and_1 (and_1_out, C_In, B);
  and and_2 (and_2_out, A, C_In);
  and and_3 (and_3_out, A, B);
  xnor xnor_1 (xnor_1_out, A, B);
  xor xor_1 (xor_1_out, B, A);
  and and_4 (and_4_out, C_In, xnor_1_out);
  and and_5 (and_5_out, not_1_out, xor_1_out);
  or or_1 (C_Out, and_1_out, and_2_out, and_3_out);
  or or_2 (Sum, and_4_out, and_5_out);

  // Notes on the sheet:
  //   C = C_IN AND (A XNOR B) OR NOTC_IN (A XOR B)
  //   C_OUT = (A AND B) OR (A AND C_IN) OR (B AND C_IN)
  //   C = C_IN AND (NOTA AND NOTB OR A AND B) OR NOTC_IN AND (NOTA AND B OR A AND NOTB)
  //   C = (NOTA AND NOTB AND C_IN) OR (A AND NOTB AND NOTC_IN) OR (NOTA AND B AND NOTC_IN) OR (A AND B AND C_IN)
endmodule

module _5BitAdder (
  input  in_1,
  input  [4:0] in_2,
  input  [4:0] in_3,
  output [4:0] sum,
  output c_out
);

  wire n1bitadder_1_c_out, n1bitadder_2_c_out, n1bitadder_3_c_out, n1bitadder_4_c_out;

  _1BitAdder u_1bitadder_1 (.C_In(in_1), .A(in_2[0]), .B(in_3[0]), .Sum(sum[0]), .C_Out(n1bitadder_1_c_out));
  _1BitAdder u_1bitadder_2 (
    .C_In(n1bitadder_1_c_out), .A(in_2[1]), .B(in_3[1]), .Sum(sum[1]), .C_Out(n1bitadder_2_c_out));
  _1BitAdder u_1bitadder_3 (
    .C_In(n1bitadder_2_c_out), .A(in_2[2]), .B(in_3[2]), .Sum(sum[2]), .C_Out(n1bitadder_3_c_out));
  _1BitAdder u_1bitadder_4 (
    .C_In(n1bitadder_3_c_out), .A(in_2[3]), .B(in_3[3]), .Sum(sum[3]), .C_Out(n1bitadder_4_c_out));
  _1BitAdder u_1bitadder_5 (.C_In(n1bitadder_4_c_out), .A(in_2[4]), .B(in_3[4]), .Sum(sum[4]), .C_Out(c_out));
endmodule

module _5BitAdderDisplay (
  input  in_1,
  input  [4:0] A,
  input  [4:0] B,
  output [6:0] out_4,
  output [6:0] out_5
);

  wire [3:0] bit_extender_1_out, bit_extender_2_out;
  wire [4:0] n5bitadder_1_sum;
  wire [5:0] divider_1_out, divider_1_rem;
  wire [5:5] n5bitadder_1_c_out;

  _5BitAdder u_5bitadder_1 (.in_1(in_1), .in_2(A), .in_3(B), .sum(n5bitadder_1_sum), .c_out(n5bitadder_1_c_out[5]));
  Divider #(.width(6)) divider_1 (
    .a({n5bitadder_1_c_out[5], n5bitadder_1_sum}), .b(6'b001010), .out(divider_1_out), .rem(divider_1_rem));  // open: upper
  Bit_Extender #(.in_width(6), .out_width(4)) bit_extender_1 (.in(divider_1_out), .out(bit_extender_1_out));
  Bit_Extender #(.in_width(6), .out_width(4)) bit_extender_2 (.in(divider_1_rem), .out(bit_extender_2_out));
  _7SegmentController u_7segmentcontroller_1 (
    .\input (bit_extender_1_out), .Top_Middle(out_4[0]), .Top_Right(out_4[1]), .Top_Left(out_4[2]),
    .Central_Middle(out_4[3]), .Bottom_Left(out_4[4]), .Bottom_Middle(out_4[5]), .Bottom_Right(out_4[6]));
  _7SegmentController u_7segmentcontroller_2 (
    .\input (bit_extender_2_out), .Top_Middle(out_5[0]), .Top_Right(out_5[1]), .Top_Left(out_5[2]),
    .Central_Middle(out_5[3]), .Bottom_Left(out_5[4]), .Bottom_Middle(out_5[5]), .Bottom_Right(out_5[6]));
endmodule

module _7Segment (
  input  [3:0] in_1
);

  wire and_1_out, and_2_out, and_3_out, and_4_out, and_5_out, and_6_out, and_7_out, and_8_out, and_9_out,
       and_10_out, and_11_out, and_12_out, and_13_out, and_14_out, and_15_out, not_1_out, not_2_out,
       or_1_out, or_2_out, or_3_out, or_4_out, or_5_out, undriven, undriven_2, undriven_3;

  not not_1 (not_1_out, in_1[2]);
  not not_2 (not_2_out, in_1[3]);
  and and_1 (and_1_out, not_1_out, not_2_out);
  and and_2 (and_2_out, in_1[2], in_1[1]);
  and and_3 (and_3_out, ~in_1[1], not_2_out, not_1_out);  // AND_Gate
  and and_4 (and_4_out, in_1[1], in_1[2]);
  and and_5 (and_5_out, not_2_out, not_1_out);
  and and_6 (and_6_out, in_1[1], in_1[3]);
  and and_7 (and_7_out, not_1_out, in_1[1]);
  and and_8 (and_8_out, in_1[0], in_1[2]);
  and and_9 (and_9_out, not_1_out, in_1[1]);
  and and_10 (and_10_out, ~in_1[1], ~in_1[3]);  // AND_Gate
  and and_11 (and_11_out, in_1[0], not_1_out);
  and and_12 (and_12_out, in_1[1], in_1[3]);
  and and_13 (and_13_out, in_1[0], in_1[1]);
  and and_14 (and_14_out, in_1[3], in_1[3]);
  or or_1 (or_1_out, and_1_out, and_2_out, and_3_out);
  or or_2 (or_2_out, and_4_out, and_5_out);
  or or_3 (or_3_out, and_6_out, and_7_out);
  and and_15 (and_15_out, and_8_out, and_9_out);
  or or_4 (or_4_out, and_11_out, and_12_out);
  or or_5 (or_5_out, and_13_out, and_14_out);
  _7_Segment_Display u_7_segment_display_1 (
    .g(undriven_2), .f(undriven_3), .a(or_1_out), .b(or_2_out), .e(and_15_out), .d(undriven), .c(or_3_out));  // open: dp

  // Notes on the sheet:
  //   not c
  //   not d
endmodule

module _7SegmentPt2 (
  input  [3:0] in_1,
  input  in_2,
  input  in_3,
  input  in_4
);

  wire and_1_out, and_2_out, and_3_out, and_4_out, and_5_out, and_6_out, and_7_out, and_8_out, and_9_out,
       and_10_out, and_11_out, and_12_out, and_13_out, or_1_out, or_2_out, or_3_out, or_4_out;

  and and_1 (and_1_out, ~in_1[2], ~in_1[0]);  // AND_Gate
  and and_2 (and_2_out, ~in_1[1], ~in_1[2], ~in_1[0]);  // AND_Gate
  and and_3 (and_3_out, ~in_1[1], ~in_1[0], in_1[2]);  // AND_Gate
  and and_4 (and_4_out, ~in_1[2], ~in_1[3]);  // AND_Gate
  and and_5 (and_5_out, in_1[1], in_1[3]);
  and and_6 (and_6_out, ~in_1[1], in_1[2]);  // AND_Gate
  and and_7 (and_7_out, ~in_1[0], ~in_1[1], ~in_1[3], ~in_1[2]);  // AND_Gate
  and and_8 (and_8_out, in_1[0], in_1[2]);
  and and_9 (and_9_out, in_1[1], ~in_1[2]);  // AND_Gate
  and and_10 (and_10_out, in_1[1], in_1[2]);
  and and_11 (and_11_out, in_1[0], in_1[1]);
  and and_12 (and_12_out, and_4_out, in_1[2]);
  and and_13 (and_13_out, in_1[2], in_1[0]);
  or or_1 (or_1_out, and_1_out, and_11_out, and_10_out, and_13_out, and_2_out);
  or or_2 (or_2_out, and_3_out, and_12_out, and_4_out);
  or or_3 (or_3_out, and_5_out, and_7_out, and_10_out, and_6_out);
  or or_4 (or_4_out, and_8_out, in_1[2], and_9_out);
  _7_Segment_Display u_7_segment_display_1 (
    .g(or_4_out), .f(or_3_out), .a(or_1_out), .b(or_2_out), .e(in_2), .d(in_4), .c(in_3));  // open: dp

  // Notes on the sheet:
  //   top middle
  //   top right
  //   top left
  //   central middle
endmodule

module _7SegmentPt3 (
  input  [3:0] in_1,
  output Top_Middle,
  output Top_Right,
  output Top_Left,
  output Central_Middle,
  output Bottom_Left,
  output Bottom_Middle,
  output Bottom_Right
);

  wire and_1_out, and_2_out, and_3_out, and_4_out, and_5_out, and_6_out, and_7_out, and_8_out, and_9_out,
       and_10_out;

  and and_1 (and_1_out, ~in_1[0], ~in_1[1], ~in_1[2], ~in_1[3]);  // AND_Gate
  and and_2 (and_2_out, in_1[0], ~in_1[1], ~in_1[2], ~in_1[3]);  // AND_Gate
  and and_3 (and_3_out, ~in_1[0], in_1[1], ~in_1[2], ~in_1[3]);  // AND_Gate
  and and_4 (and_4_out, in_1[0], in_1[1], ~in_1[2], ~in_1[3]);  // AND_Gate
  and and_5 (and_5_out, ~in_1[0], ~in_1[1], in_1[2], ~in_1[3]);  // AND_Gate
  and and_6 (and_6_out, in_1[0], ~in_1[1], in_1[2], ~in_1[3]);  // AND_Gate
  and and_7 (and_7_out, ~in_1[0], in_1[1], in_1[2], ~in_1[3]);  // AND_Gate
  and and_8 (and_8_out, in_1[0], in_1[1], in_1[2], ~in_1[3]);  // AND_Gate
  and and_9 (and_9_out, ~in_1[0], ~in_1[1], ~in_1[2], in_1[3]);  // AND_Gate
  and and_10 (and_10_out, in_1[0], ~in_1[1], ~in_1[2], in_1[3]);  // AND_Gate
  or or_1 (Top_Middle, and_1_out, and_3_out, and_4_out, and_6_out, and_7_out, and_8_out, and_9_out, and_10_out);
  or or_2 (Top_Right, and_1_out, and_2_out, and_9_out, and_3_out, and_4_out, and_5_out, and_8_out, and_10_out);
  or or_3 (Top_Left, and_1_out, and_5_out, and_6_out, and_7_out, and_9_out, and_10_out);
  or or_4 (Central_Middle, and_3_out, and_4_out, and_5_out, and_6_out, and_7_out, and_9_out, and_10_out);
  or or_5 (Bottom_Left, and_1_out, and_3_out, and_7_out, and_9_out);
  or or_6 (Bottom_Middle, and_1_out, and_3_out, and_4_out, and_6_out, and_7_out, and_9_out, and_10_out);
  or or_7 (Bottom_Right, and_1_out, and_2_out, and_4_out, and_5_out, and_6_out, and_7_out, and_8_out, and_9_out, and_10_out);
endmodule

module _7SegmentController (
  input  [3:0] \input ,
  output Top_Middle,
  output Top_Right,
  output Top_Left,
  output Central_Middle,
  output Bottom_Left,
  output Bottom_Middle,
  output Bottom_Right
);

  wire comparator_1_gt;
  wire [3:0] multiplexer_1_out;

  Multiplexer #(.width(4), .enable("false")) multiplexer_1 (
    .in0(4'b0000), .in1(\input ), .out(multiplexer_1_out), .sel(comparator_1_gt));
  Comparator #(.width(4)) comparator_1 (.a(\input ), .b(4'b1010), .gt(comparator_1_gt));  // open: eq, lt
  _7SegmentPt3 u_7segmentpt3_1 (
    .in_1(multiplexer_1_out), .Top_Middle(Top_Middle), .Top_Right(Top_Right), .Top_Left(Top_Left),
    .Central_Middle(Central_Middle), .Bottom_Left(Bottom_Left), .Bottom_Middle(Bottom_Middle),
    .Bottom_Right(Bottom_Right));
endmodule
