// Logisim project Addyelle_Dizon.circ as structural Verilog: 1 circuit, main circuit main
module main (
  input  a,
  input  b,
  input  c,
  input  d,
  input  selection_1,
  input  selection_2,
  output out_7
);

  wire and_1_out, and_2_out, and_3_out, and_4_out, or_1_out, or_2_out;

  and and_1 (and_1_out, a, ~selection_1, ~selection_2);  // AND_Gate
  and and_2 (and_2_out, b, ~selection_1, selection_2);  // AND_Gate
  and and_3 (and_3_out, c, selection_1, ~selection_2);  // AND_Gate
  and and_4 (and_4_out, d, selection_1, selection_2);
  or or_1 (or_1_out, and_1_out, and_2_out);
  or or_2 (or_2_out, and_3_out, and_4_out);
  or or_3 (out_7, or_1_out, or_2_out);

  // Notes on the sheet:
  //   I didn't really know what the question meant, so I assumed that if the selection bits are 00, then the signal that should output is A,
  //   if the selection bits are 01, then the signal that should output is B
  //   if the selection bits are 10, then the signal that should output is C
  //   if the selection bits are 11, then the signal that should output is D
endmodule
