// Logisim project ClockFinal.circ as structural Verilog: 12 circuits, main circuit 4BitCounter
module main (
  input  in_1
);

  wire clock_1_out;
  wire [6:0] clockcontroller_1_am_pm, clockcontroller_1_hr_ones, clockcontroller_1_hr_tens,
       clockcontroller_1_min_ones, clockcontroller_1_min_tens;

  ClockController clockcontroller_1 (
    .clock(clock_1_out), .enable(in_1), .hr_tens(clockcontroller_1_hr_tens),
    .hr_ones(clockcontroller_1_hr_ones), .min_tens(clockcontroller_1_min_tens),
    .min_ones(clockcontroller_1_min_ones), .am_pm(clockcontroller_1_am_pm));
  Clock clock_1 (.out(clock_1_out));
  _7_Segment_Display u_7_segment_display_1 (
    .g(clockcontroller_1_hr_ones[3]), .f(clockcontroller_1_hr_ones[2]), .a(clockcontroller_1_hr_ones[0]),
    .b(clockcontroller_1_hr_ones[1]), .e(clockcontroller_1_hr_ones[4]), .d(clockcontroller_1_hr_ones[5]),
    .c(clockcontroller_1_hr_ones[6]));  // open: dp
  _7_Segment_Display u_7_segment_display_2 (
    .g(clockcontroller_1_hr_tens[3]), .f(clockcontroller_1_hr_tens[2]), .a(clockcontroller_1_hr_tens[0]),
    .b(clockcontroller_1_hr_tens[1]), .e(clockcontroller_1_hr_tens[4]), .d(clockcontroller_1_hr_tens[5]),
    .c(clockcontroller_1_hr_tens[6]));  // open: dp
  _7_Segment_Display u_7_segment_display_3 (
    .g(clockcontroller_1_min_ones[3]), .f(clockcontroller_1_min_ones[2]), .a(clockcontroller_1_min_ones[0]),
    .b(clockcontroller_1_min_ones[1]), .e(clockcontroller_1_min_ones[4]), .d(clockcontroller_1_min_ones[5]),
    .c(clockcontroller_1_min_ones[6]));  // open: dp
  _7_Segment_Display u_7_segment_display_4 (
    .g(clockcontroller_1_min_tens[3]), .f(clockcontroller_1_min_tens[2]), .a(clockcontroller_1_min_tens[0]),
    .b(clockcontroller_1_min_tens[1]), .e(clockcontroller_1_min_tens[4]), .d(clockcontroller_1_min_tens[5]),
    .c(clockcontroller_1_min_tens[6]));  // open: dp
  _7_Segment_Display u_7_segment_display_5 (
    .g(clockcontroller_1_am_pm[3]), .f(clockcontroller_1_am_pm[2]), .a(clockcontroller_1_am_pm[0]),
    .b(clockcontroller_1_am_pm[1]), .e(clockcontroller_1_am_pm[4]), .d(clockcontroller_1_am_pm[5]),
    .c(clockcontroller_1_am_pm[6]));  // open: dp
endmodule

module _1BitCounter_for_AM_PM (
  input  clock,
  input  enable,
  output out_3
);

  wire adder_1_out, multiplexer_1_out;

  Adder #(.width(1)) adder_1 (.a(1'b1), .b(out_3), .out(adder_1_out));  // open: cin, cout
  Multiplexer #(.enable("false")) multiplexer_1 (
    .in1(adder_1_out), .out(multiplexer_1_out), .sel(enable));  // open: in0
  D_Flip_Flop d_ff_1 (.clk(clock), .D(multiplexer_1_out), .Q(out_3));  // open: Qn, preset, en, reset
endmodule

module _4BitCounter (
  input  clock,
  input  enable,
  output [3:0] out_3,
  output out_4,
  output _11_59_59
);

  wire [3:0] adder_1_out, multiplexer_1_out;

  Adder #(.width(4)) adder_1 (.a(4'b0001), .b(out_3), .out(adder_1_out));  // open: cin, cout
  Multiplexer #(.width(4), .enable("false")) multiplexer_1 (
    .in1(adder_1_out), .out(multiplexer_1_out), .sel(enable));  // open: in0
  D_Flip_Flop d_ff_1 (.clk(clock), .D(multiplexer_1_out[0]), .Q(out_3[0]), .preset(out_4));  // open: Qn, en, reset
  D_Flip_Flop d_ff_2 (.clk(clock), .D(multiplexer_1_out[1]), .Q(out_3[1]), .reset(out_4));  // open: Qn, preset, en
  D_Flip_Flop d_ff_3 (.clk(clock), .D(multiplexer_1_out[2]), .Q(out_3[2]), .reset(out_4));  // open: Qn, preset, en
  D_Flip_Flop d_ff_4 (.clk(clock), .D(multiplexer_1_out[3]), .Q(out_3[3]), .reset(out_4));  // open: Qn, preset, en
  Comparator #(.width(4)) comparator_1 (.a(out_3), .b(4'b1101), .eq(out_4));  // open: gt, lt
  Comparator #(.width(4)) comparator_2 (.a(out_3), .b(4'b1011), .eq(_11_59_59));  // open: gt, lt
endmodule

module _4BitDecoder (
  input  clock,
  input  enable,
  output [6:0] out_3,
  output [6:0] out_4,
  output _12_59_59
);

  wire [3:0] bit_extender_1_out, bit_extender_2_out, divider_1_out, divider_1_rem, n4bitcounter_1_out_3;

  _4BitCounter u_4bitcounter_1 (
    .clock(clock), .enable(enable), .out_3(n4bitcounter_1_out_3), ._11_59_59(_12_59_59));  // open: out_4
  Divider #(.width(4)) divider_1 (
    .a(n4bitcounter_1_out_3), .b(4'b1010), .out(divider_1_out), .rem(divider_1_rem));  // open: upper
  Bit_Extender #(.in_width(4), .out_width(4)) bit_extender_1 (.in(divider_1_out), .out(bit_extender_1_out));
  Bit_Extender #(.in_width(4), .out_width(4)) bit_extender_2 (.in(divider_1_rem), .out(bit_extender_2_out));
  _7SegmentController u_7segmentcontroller_1 (
    .\input (bit_extender_1_out), .Top_Middle(out_3[0]), .Top_Right(out_3[1]), .Top_Left(out_3[2]),
    .Central_Middle(out_3[3]), .Bottom_Left(out_3[4]), .Bottom_Middle(out_3[5]), .Bottom_Right(out_3[6]));
  _7SegmentController u_7segmentcontroller_2 (
    .\input (bit_extender_2_out), .Top_Middle(out_4[0]), .Top_Right(out_4[1]), .Top_Left(out_4[2]),
    .Central_Middle(out_4[3]), .Bottom_Left(out_4[4]), .Bottom_Middle(out_4[5]), .Bottom_Right(out_4[6]));
endmodule

module _6BitCounter (
  input  clock,
  input  enable,
  output [5:0] Output,
  output _59_out,
  output _60_out
);

  wire [5:0] adder_1_out, multiplexer_1_out;

  Adder #(.width(6)) adder_1 (.a(6'b000001), .b(Output), .out(adder_1_out));  // open: cin, cout
  Multiplexer #(.width(6), .enable("false")) multiplexer_1 (
    .in1(adder_1_out), .out(multiplexer_1_out), .sel(enable));  // open: in0
  D_Flip_Flop d_ff_1 (.clk(clock), .D(multiplexer_1_out[0]), .Q(Output[0]), .reset(_60_out));  // open: Qn, preset, en
  D_Flip_Flop d_ff_2 (.clk(clock), .D(multiplexer_1_out[1]), .Q(Output[1]), .reset(_60_out));  // open: Qn, preset, en
  D_Flip_Flop d_ff_3 (.clk(clock), .D(multiplexer_1_out[2]), .Q(Output[2]), .reset(_60_out));  // open: Qn, preset, en
  D_Flip_Flop d_ff_4 (.clk(clock), .D(multiplexer_1_out[3]), .Q(Output[3]), .reset(_60_out));  // open: Qn, preset, en
  D_Flip_Flop d_ff_5 (.clk(clock), .D(multiplexer_1_out[4]), .Q(Output[4]), .reset(_60_out));  // open: Qn, preset, en
  D_Flip_Flop d_ff_6 (.clk(clock), .D(multiplexer_1_out[5]), .Q(Output[5]), .reset(_60_out));  // open: Qn, preset, en
  Comparator #(.width(6)) comparator_1 (.a(Output), .b(6'b111100), .eq(_60_out));  // open: gt, lt
  Comparator #(.width(6)) comparator_2 (.a(Output), .b(6'b111011), .eq(_59_out));  // open: gt, lt
endmodule

module _6BitDecoder (
  input  clock,
  input  enable,
  output [6:0] out_3,
  output [6:0] out_4,
  output increment
);

  wire [3:0] bit_extender_1_out, bit_extender_2_out;
  wire [5:0] divider_1_out, divider_1_rem, n6bitcounter_1_output;

  _6BitCounter u_6bitcounter_1 (
    .clock(clock), .enable(enable), .Output(n6bitcounter_1_output), ._59_out(increment));  // open: _60_out
  Divider #(.width(6)) divider_1 (
    .a(n6bitcounter_1_output), .b(6'b001010), .out(divider_1_out), .rem(divider_1_rem));  // open: upper
  Bit_Extender #(.in_width(6), .out_width(4)) bit_extender_1 (.in(divider_1_out), .out(bit_extender_1_out));
  Bit_Extender #(.in_width(6), .out_width(4)) bit_extender_2 (.in(divider_1_rem), .out(bit_extender_2_out));
  _7SegmentController u_7segmentcontroller_1 (
    .\input (bit_extender_1_out), .Top_Middle(out_3[0]), .Top_Right(out_3[1]), .Top_Left(out_3[2]),
    .Central_Middle(out_3[3]), .Bottom_Left(out_3[4]), .Bottom_Middle(out_3[5]), .Bottom_Right(out_3[6]));
  _7SegmentController u_7segmentcontroller_2 (
    .\input (bit_extender_2_out), .Top_Middle(out_4[0]), .Top_Right(out_4[1]), .Top_Left(out_4[2]),
    .Central_Middle(out_4[3]), .Bottom_Left(out_4[4]), .Bottom_Middle(out_4[5]), .Bottom_Right(out_4[6]));
endmodule

module _7Segment (
  input  [3:0] in_1,
  output Top_Middle,
  output Top_Right,
  output Top_Left,
  output Central_Middle,
  output Bottom_Left,
  output Bottom_Middle,
  output Bottom_Right
);

  wire and_1_out, and_2_out, and_3_out, and_4_out, and_5_out, and_6_out, and_7_out, and_8_out, and_9_out,
       and_10_out;

  and and_1 (and_1_out, ~in_1[0], ~in_1[1], ~in_1[2], ~in_1[3]);  // AND_Gate
  and and_2 (and_2_out, in_1[0], ~in_1[1], ~in_1[2], ~in_1[3]);  // AND_Gate
  and and_3 (and_3_out, ~in_1[0], in_1[1], ~in_1[2], ~in_1[3]);  // AND_Gate
  and and_4 (and_4_out, in_1[0], in_1[1], ~in_1[2], ~in_1[3]);  // AND_Gate
  and and_5 (and_5_out, ~in_1[0], ~in_1[1], in_1[2], ~in_1[3]);  // AND_Gate
  and and_6 (and_6_out, in_1[0], ~in_1[1], in_1[2], ~in_1[3]);  // AND_Gate
  and and_7 (and_7_out, ~in_1[0], in_1[1], in_1[2], ~in_1[3]);  // AND_Gate
  and and_8 (and_8_out, in_1[0], in_1[1], in_1[2], ~in_1[3]);  // AND_Gate
  and and_9 (and_9_out, ~in_1[0], ~in_1[1], ~in_1[2], in_1[3]);  // AND_Gate
  and and_10 (and_10_out, in_1[0], ~in_1[1], ~in_1[2], in_1[3]);  // AND_Gate
  or or_1 (Top_Middle, and_1_out, and_3_out, and_4_out, and_6_out, and_7_out, and_8_out, and_9_out, and_10_out);
  or or_2 (Top_Right, and_1_out, and_2_out, and_9_out, and_3_out, and_4_out, and_5_out, and_8_out, and_10_out);
  or or_3 (Top_Left, and_1_out, and_5_out, and_6_out, and_7_out, and_9_out, and_10_out);
  or or_4 (Central_Middle, and_3_out, and_4_out, and_5_out, and_6_out, and_7_out, and_9_out, and_10_out);
  or or_5 (Bottom_Left, and_1_out, and_3_out, and_7_out, and_9_out);
  or or_6 (Bottom_Middle, and_1_out, and_3_out, and_4_out, and_6_out, and_7_out, and_9_out, and_10_out);
  or or_7 (Bottom_Right, and_1_out, and_2_out, and_4_out, and_5_out, and_6_out, and_7_out, and_8_out, and_9_out, and_10_out);
endmodule

module _7SegmentController (
  input  [3:0] \input ,
  output Top_Middle,
  output Top_Right,
  output Top_Left,
  output Central_Middle,
  output Bottom_Left,
  output Bottom_Middle,
  output Bottom_Right
);

  wire comparator_1_lt;
  wire [3:0] multiplexer_1_out;

  Comparator #(.width(4), .mode("unsigned")) comparator_1 (
    .a(\input ), .b(4'b1010), .lt(comparator_1_lt));  // open: gt, eq
  Multiplexer #(.width(4), .disabled(0), .enable("false")) multiplexer_1 (
    .in0(4'b0000), .in1(\input ), .out(multiplexer_1_out), .sel(comparator_1_lt));
  _7Segment u_7segment_1 (
    .in_1(multiplexer_1_out), .Top_Middle(Top_Middle), .Top_Right(Top_Right), .Top_Left(Top_Left),
    .Central_Middle(Central_Middle), .Bottom_Left(Bottom_Left), .Bottom_Middle(Bottom_Middle),
    .Bottom_Right(Bottom_Right));
endmodule

module AMPMSegment (
  input  in_1,
  output Top_Middle,
  output Top_Right,
  output Top_Left,
  output Central_Middle,
  output Bottom_Left,
  output Bottom_Middle,
  output Bottom_Right
);

  wire and_1_out, and_2_out, undriven;

  and and_1 (and_1_out, ~in_1, ~in_1, ~in_1, ~in_1);  // AND_Gate
  and and_2 (and_2_out, in_1, in_1, in_1, in_1);
  or or_1 (Top_Middle, and_1_out, and_2_out);
  or or_2 (Top_Right, and_1_out, and_2_out);
  or or_3 (Top_Left, and_1_out, and_2_out);
  or or_4 (Central_Middle, and_1_out, and_2_out);
  or or_5 (Bottom_Left, and_1_out, and_2_out);
  buf or_6 (Bottom_Middle, undriven);  // OR_Gate
  buf or_7 (Bottom_Right, and_1_out);  // OR_Gate
endmodule

module ClockCounter (
  input  clock,
  input  enable,
  output [5:0] seconds,
  output _00_00_59,
  output [5:0] minutes,
  output _00_59_00,
  output [3:0] hours,
  output _11_00_00,
  output am_pm_or_pm_am_changer
);

  wire n6bitcounter_2__60_out;

  _6BitCounter u_6bitcounter_1 (
    .clock(clock), .enable(enable), .Output(seconds), ._59_out(_00_00_59));  // open: _60_out
  _6BitCounter u_6bitcounter_2 (
    .clock(clock), .enable(_00_00_59), .Output(minutes), ._59_out(_00_59_00), ._60_out(n6bitcounter_2__60_out));
  _4BitCounter u_4bitcounter_1 (
    .clock(n6bitcounter_2__60_out), .enable(enable), .out_3(hours), ._11_59_59(_11_00_00));  // open: out_4
  and and_1 (am_pm_or_pm_am_changer, _00_00_59, _00_59_00, _11_00_00);
endmodule

module ClockDecoder (
  input  clock,
  input  enable,
  output [6:0] out_3,
  output [6:0] out_4,
  output [6:0] out_5,
  output [6:0] out_6,
  output [6:0] out_7
);

  wire clockcounter_1_am_pm_or_pm_am_changer, n1bitcounter_for_am_pm_1_out_3;
  wire [3:0] bit_extender_1_out, bit_extender_2_out, bit_extender_3_out, bit_extender_4_out,
       clockcounter_1_hours, divider_1_out, divider_1_rem;
  wire [5:0] clockcounter_1_minutes, divider_2_out, divider_2_rem;

  ClockCounter clockcounter_1 (
    .clock(clock), .enable(enable), .minutes(clockcounter_1_minutes), .hours(clockcounter_1_hours),
    .am_pm_or_pm_am_changer(clockcounter_1_am_pm_or_pm_am_changer));  // open: seconds, _00_00_59, _00_59_00, _11_00_00
  Divider #(.width(4)) divider_1 (
    .a(clockcounter_1_hours), .b(4'b1010), .out(divider_1_out), .rem(divider_1_rem));  // open: upper
  Divider #(.width(6)) divider_2 (
    .a(clockcounter_1_minutes), .b(6'b001010), .out(divider_2_out), .rem(divider_2_rem));  // open: upper
  _1BitCounter_for_AM_PM u_1bitcounter_for_am_pm_1 (
    .clock(clock), .enable(clockcounter_1_am_pm_or_pm_am_changer), .out_3(n1bitcounter_for_am_pm_1_out_3));
  Bit_Extender #(.in_width(4), .out_width(4)) bit_extender_1 (.in(divider_1_out), .out(bit_extender_1_out));
  Bit_Extender #(.in_width(4), .out_width(4)) bit_extender_2 (.in(divider_1_rem), .out(bit_extender_2_out));
  Bit_Extender #(.in_width(6), .out_width(4)) bit_extender_3 (.in(divider_2_out), .out(bit_extender_3_out));
  Bit_Extender #(.in_width(6), .out_width(4)) bit_extender_4 (.in(divider_2_rem), .out(bit_extender_4_out));
  _7SegmentController u_7segmentcontroller_1 (
    .\input (bit_extender_1_out), .Top_Middle(out_3[0]), .Top_Right(out_3[1]), .Top_Left(out_3[2]),
    .Central_Middle(out_3[3]), .Bottom_Left(out_3[4]), .Bottom_Middle(out_3[5]), .Bottom_Right(out_3[6]));
  _7SegmentController u_7segmentcontroller_2 (
    .\input (bit_extender_2_out), .Top_Middle(out_4[0]), .Top_Right(out_4[1]), .Top_Left(out_4[2]),
    .Central_Middle(out_4[3]), .Bottom_Left(out_4[4]), .Bottom_Middle(out_4[5]), .Bottom_Right(out_4[6]));
  _7Segment u_7segment_1 (
    .in_1(bit_extender_3_out), .Top_Middle(out_5[0]), .Top_Right(out_5[1]), .Top_Left(out_5[2]),
    .Central_Middle(out_5[3]), .Bottom_Left(out_5[4]), .Bottom_Middle(out_5[5]), .Bottom_Right(out_5[6]));
  _7Segment u_7segment_2 (
    .in_1(bit_extender_4_out), .Top_Middle(out_6[0]), .Top_Right(out_6[1]), .Top_Left(out_6[2]),
    .Central_Middle(out_6[3]), .Bottom_Left(out_6[4]), .Bottom_Middle(out_6[5]), .Bottom_Right(out_6[6]));
  AMPMSegment ampmsegment_1 (
    .in_1(n1bitcounter_for_am_pm_1_out_3), .Top_Middle(out_7[0]), .Top_Right(out_7[1]), .Top_Left(out_7[2]),
    .Central_Middle(out_7[3]), .Bottom_Left(out_7[4]), .Bottom_Middle(out_7[5]), .Bottom_Right(out_7[6]));
endmodule

module ClockController (
  input  clock,
  input  enable,
  output [6:0] hr_tens,
  output [6:0] hr_ones,
  output [6:0] min_tens,
  output [6:0] min_ones,
  output [6:0] am_pm
);

  ClockDecoder clockdecoder_1 (
    .clock(clock), .enable(enable), .out_3(hr_tens), .out_4(hr_ones), .out_5(min_tens), .out_6(min_ones),
    .out_7(am_pm));
endmodule
