// Logisim project ClockMinutes.circ as structural Verilog: 7 circuits, main circuit main
module main (
  input  Enable
);

  wire Clock_out;
  wire [6:0] minutedecoder_1_out_3, minutedecoder_1_out_4;

  Clock Clock (.out(Clock_out));
  MinuteDecoder minutedecoder_1 (
    .clock(Clock_out), .enable(Enable), .out_3(minutedecoder_1_out_3), .out_4(minutedecoder_1_out_4));
  _7_Segment_Display u_7_segment_display_1 (
    .g(minutedecoder_1_out_3[3]), .f(minutedecoder_1_out_3[2]), .a(minutedecoder_1_out_3[0]),
    .b(minutedecoder_1_out_3[1]), .e(minutedecoder_1_out_3[4]), .d(minutedecoder_1_out_3[5]),
    .c(minutedecoder_1_out_3[6]));  // open: dp
  _7_Segment_Display u_7_segment_display_2 (
    .g(minutedecoder_1_out_4[3]), .f(minutedecoder_1_out_4[2]), .a(minutedecoder_1_out_4[0]),
    .b(minutedecoder_1_out_4[1]), .e(minutedecoder_1_out_4[4]), .d(minutedecoder_1_out_4[5]),
    .c(minutedecoder_1_out_4[6]));  // open: dp
endmodule

module _6BitCounter (
  input  clock,
  input  enable,
  output [5:0] Output,
  output _60_out
);

  wire comparator_1_eq;
  wire [5:0] adder_1_out, multiplexer_1_out;

  Adder #(.width(6)) adder_1 (.a(6'b000001), .b(Output), .out(adder_1_out));  // open: cin, cout
  Multiplexer #(.width(6), .enable("false")) multiplexer_1 (
    .in1(adder_1_out), .out(multiplexer_1_out), .sel(enable));  // open: in0
  D_Flip_Flop d_ff_1 (
    .clk(clock), .D(multiplexer_1_out[0]), .Q(Output[0]), .reset(comparator_1_eq));  // open: Qn, preset, en
  D_Flip_Flop d_ff_2 (
    .clk(clock), .D(multiplexer_1_out[1]), .Q(Output[1]), .reset(comparator_1_eq));  // open: Qn, preset, en
  D_Flip_Flop d_ff_3 (
    .clk(clock), .D(multiplexer_1_out[2]), .Q(Output[2]), .reset(comparator_1_eq));  // open: Qn, preset, en
  D_Flip_Flop d_ff_4 (
    .clk(clock), .D(multiplexer_1_out[3]), .Q(Output[3]), .reset(comparator_1_eq));  // open: Qn, preset, en
  D_Flip_Flop d_ff_5 (
    .clk(clock), .D(multiplexer_1_out[4]), .Q(Output[4]), .reset(comparator_1_eq));  // open: Qn, preset, en
  D_Flip_Flop d_ff_6 (
    .clk(clock), .D(multiplexer_1_out[5]), .Q(Output[5]), .reset(comparator_1_eq));  // open: Qn, preset, en
  Comparator #(.width(6)) comparator_1 (.a(Output), .b(6'b111100), .eq(comparator_1_eq));  // open: gt, lt
  Comparator #(.width(6)) comparator_2 (.a(Output), .b(6'b111011), .eq(_60_out));  // open: gt, lt
endmodule

module _6BitDecoder (
  input  clock,
  input  enable,
  output [6:0] out_3,
  output [6:0] out_4,
  output increment
);

  wire [3:0] bit_extender_1_out, bit_extender_2_out;
  wire [5:0] divider_1_out, divider_1_rem, n6bitcounter_1_output;

  _6BitCounter u_6bitcounter_1 (.clock(clock), .enable(enable), .Output(n6bitcounter_1_output), ._60_out(increment));
  Divider #(.width(6)) divider_1 (
    .a(n6bitcounter_1_output), .b(6'b001010), .out(divider_1_out), .rem(divider_1_rem));  // open: upper
  Bit_Extender #(.in_width(6), .out_width(4)) bit_extender_1 (.in(divider_1_out), .out(bit_extender_1_out));
  Bit_Extender #(.in_width(6), .out_width(4)) bit_extender_2 (.in(divider_1_rem), .out(bit_extender_2_out));
  _7SegmentController u_7segmentcontroller_1 (
    .\input (bit_extender_1_out), .Top_Middle(out_3[0]), .Top_Right(out_3[1]), .Top_Left(out_3[2]),
    .Central_Middle(out_3[3]), .Bottom_Left(out_3[4]), .Bottom_Middle(out_3[5]), .Bottom_Right(out_3[6]));
  _7SegmentController u_7segmentcontroller_2 (
    .\input (bit_extender_2_out), .Top_Middle(out_4[0]), .Top_Right(out_4[1]), .Top_Left(out_4[2]),
    .Central_Middle(out_4[3]), .Bottom_Left(out_4[4]), .Bottom_Middle(out_4[5]), .Bottom_Right(out_4[6]));
endmodule

module _7Segment (
  input  [3:0] in_1,
  output Top_Middle,
  output Top_Right,
  output Top_Left,
  output Central_Middle,
  output Bottom_Left,
  output Bottom_Middle,
  output Bottom_Right
);

  wire and_1_out, and_2_out, and_3_out, and_4_out, and_5_out, and_6_out, and_7_out, and_8_out, and_9_out,
       and_10_out;

  and and_1 (and_1_out, ~in_1[0], ~in_1[1], ~in_1[2], ~in_1[3]);  // AND_Gate
  and and_2 (and_2_out, in_1[0], ~in_1[1], ~in_1[2], ~in_1[3]);  // AND_Gate
  and and_3 (and_3_out, ~in_1[0], in_1[1], ~in_1[2], ~in_1[3]);  // AND_Gate
  and and_4 (and_4_out, in_1[0], in_1[1], ~in_1[2], ~in_1[3]);  // AND_Gate
  and and_5 (and_5_out, ~in_1[0], ~in_1[1], in_1[2], ~in_1[3]);  // AND_Gate
  and and_6 (and_6_out, in_1[0], ~in_1[1], in_1[2], ~in_1[3]);  // AND_Gate
  and and_7 (and_7_out, ~in_1[0], in_1[1], in_1[2], ~in_1[3]);  // AND_Gate
  and and_8 (and_8_out, in_1[0], in_1[1], in_1[2], ~in_1[3]);  // AND_Gate
  and and_9 (and_9_out, ~in_1[0], ~in_1[1], ~in_1[2], in_1[3]);  // AND_Gate
  and and_10 (and_10_out, in_1[0], ~in_1[1], ~in_1[2], in_1[3]);  // AND_Gate
  or or_1 (Top_Middle, and_1_out, and_3_out, and_4_out, and_6_out, and_7_out, and_8_out, and_9_out, and_10_out);
  or or_2 (Top_Right, and_1_out, and_2_out, and_9_out, and_3_out, and_4_out, and_5_out, and_8_out, and_10_out);
  or or_3 (Top_Left, and_1_out, and_5_out, and_6_out, and_7_out, and_9_out, and_10_out);
  or or_4 (Central_Middle, and_3_out, and_4_out, and_5_out, and_6_out, and_7_out, and_9_out, and_10_out);
  or or_5 (Bottom_Left, and_1_out, and_3_out, and_7_out, and_9_out);
  or or_6 (Bottom_Middle, and_1_out, and_3_out, and_4_out, and_6_out, and_7_out, and_9_out, and_10_out);
  or or_7 (Bottom_Right, and_1_out, and_2_out, and_4_out, and_5_out, and_6_out, and_7_out, and_8_out, and_9_out, and_10_out);
endmodule

module _7SegmentController (
  input  [3:0] \input ,
  output Top_Middle,
  output Top_Right,
  output Top_Left,
  output Central_Middle,
  output Bottom_Left,
  output Bottom_Middle,
  output Bottom_Right
);

  wire comparator_1_lt;
  wire [3:0] multiplexer_1_out;

  Comparator #(.width(4), .mode("unsigned")) comparator_1 (
    .a(\input ), .b(4'b1010), .lt(comparator_1_lt));  // open: gt, eq
  Multiplexer #(.width(4), .disabled(0), .enable("false")) multiplexer_1 (
    .in0(4'b0000), .in1(\input ), .out(multiplexer_1_out), .sel(comparator_1_lt));
  _7Segment u_7segment_1 (
    .in_1(multiplexer_1_out), .Top_Middle(Top_Middle), .Top_Right(Top_Right), .Top_Left(Top_Left),
    .Central_Middle(Central_Middle), .Bottom_Left(Bottom_Left), .Bottom_Middle(Bottom_Middle),
    .Bottom_Right(Bottom_Right));
endmodule

module MinuteCounter (
  input  Clock,
  input  Enable,
  output [5:0] out_3
);

  wire n6bitcounter_1__60_out;

  _6BitCounter u_6bitcounter_1 (.clock(Clock), .enable(Enable), ._60_out(n6bitcounter_1__60_out));  // open: Output
  _6BitCounter u_6bitcounter_2 (.clock(Clock), .enable(n6bitcounter_1__60_out), .Output(out_3));  // open: _60_out
endmodule

module MinuteDecoder (
  input  clock,
  input  enable,
  output [6:0] out_3,
  output [6:0] out_4
);

  wire [3:0] bit_extender_1_out, bit_extender_2_out;
  wire [5:0] divider_1_out, divider_1_rem, minutecounter_1_out_3;

  MinuteCounter minutecounter_1 (.Clock(clock), .Enable(enable), .out_3(minutecounter_1_out_3));
  Divider #(.width(6)) divider_1 (
    .a(minutecounter_1_out_3), .b(6'b001010), .out(divider_1_out), .rem(divider_1_rem));  // open: upper
  Bit_Extender #(.in_width(6), .out_width(4)) bit_extender_1 (.in(divider_1_out), .out(bit_extender_1_out));
  Bit_Extender #(.in_width(6), .out_width(4)) bit_extender_2 (.in(divider_1_rem), .out(bit_extender_2_out));
  _7SegmentController u_7segmentcontroller_1 (
    .\input (bit_extender_1_out), .Top_Middle(out_3[0]), .Top_Right(out_3[1]), .Top_Left(out_3[2]),
    .Central_Middle(out_3[3]), .Bottom_Left(out_3[4]), .Bottom_Middle(out_3[5]), .Bottom_Right(out_3[6]));
  _7SegmentController u_7segmentcontroller_2 (
    .\input (bit_extender_2_out), .Top_Middle(out_4[0]), .Top_Right(out_4[1]), .Top_Left(out_4[2]),
    .Central_Middle(out_4[3]), .Bottom_Left(out_4[4]), .Bottom_Middle(out_4[5]), .Bottom_Right(out_4[6]));
endmodule
