// Logisim project CountingCirc.circ as structural Verilog: 2 circuits, main circuit main
module main (
  input  in_1,
  output [4:0] out_2
);

  wire clock_1_out;

  Clock clock_1 (.out(clock_1_out));
  _5BitCounting u_5bitcounting_1 (.clock(clock_1_out), .enable(in_1), .Output(out_2));

  // Notes on the sheet:
  //   Press change enable pin to 1 to enable the clock
endmodule

module _5BitCounting (
  input  clock,
  input  enable,
  output [4:0] Output
);

  wire [4:0] adder_1_out, multiplexer_1_out;

  Adder #(.width(5)) adder_1 (.a(5'b00001), .b(Output), .out(adder_1_out));  // open: cin, cout
  Multiplexer #(.width(5), .enable("false")) multiplexer_1 (
    .in1(adder_1_out), .out(multiplexer_1_out), .sel(enable));  // open: in0
  D_Flip_Flop d_ff_1 (.clk(clock), .D(multiplexer_1_out[0]), .Q(Output[0]));  // open: Qn, preset, en, reset
  D_Flip_Flop d_ff_2 (.clk(clock), .D(multiplexer_1_out[1]), .Q(Output[1]));  // open: Qn, preset, en, reset
  D_Flip_Flop d_ff_3 (.clk(clock), .D(multiplexer_1_out[2]), .Q(Output[2]));  // open: Qn, preset, en, reset
  D_Flip_Flop d_ff_4 (.clk(clock), .D(multiplexer_1_out[3]), .Q(Output[3]));  // open: Qn, preset, en, reset
  D_Flip_Flop d_ff_5 (.clk(clock), .D(multiplexer_1_out[4]), .Q(Output[4]));  // open: Qn, preset, en, reset
endmodule
